// Logisim project snake.circ as structural Verilog: 14 circuits, main circuit registerGroup
module main (
);

  wire button_1_out, button_2_out, button_3_out, button_4_out, button_5_out, instructionset_1_reverse,
       \instructionset_1_显卡缓存 , \instructionset_1_显卡读入 ;
  wire [3:0] \得分数字显示控制_out_3 , \得分数字显示控制_out_3_2 , \显示处理_x ;
  wire [7:0] cpu_1_io1, cpu_1_io2, screen_interface_1_out_3, screen_interface_1_out_4,
       screen_interface_1_out_5, screen_interface_1_out_6, screen_interface_1_out_7,
       screen_interface_1_out_8, screen_interface_1_out_9, screen_interface_1_out_10,
       screen_interface_2_out_3, screen_interface_2_out_4, screen_interface_2_out_5,
       screen_interface_2_out_6, screen_interface_2_out_7, screen_interface_2_out_8,
       screen_interface_2_out_9, screen_interface_2_out_10, screen_interface_3_out_3,
       screen_interface_3_out_4, screen_interface_3_out_5, screen_interface_3_out_6,
       screen_interface_3_out_7, screen_interface_3_out_8, screen_interface_3_out_9,
       screen_interface_3_out_10, screen_interface_4_out_3, screen_interface_4_out_4,
       screen_interface_4_out_5, screen_interface_4_out_6, screen_interface_4_out_7,
       screen_interface_4_out_8, screen_interface_4_out_9, screen_interface_4_out_10, \显示处理_down , \显示处理_up ;
  wire [15:0] cpu_1_instruction_out;
  wire [31:0] keybroad_1_out_code, \屏幕驱动_2_out_1 , \屏幕驱动_2_out_2 , \屏幕驱动_2_out_3 , \屏幕驱动_2_out_4 ,
       \屏幕驱动_out_1 , \屏幕驱动_out_2 , \屏幕驱动_out_3 , \屏幕驱动_out_4 ;

  Button button_1 (.out(button_1_out));
  keybroad keybroad_1 (
    .BTN_UP(button_2_out), .BTN_LEFT(button_3_out), .BTN_right(button_5_out), .BTN_DOWN(button_4_out),
    .OUT_CODE(keybroad_1_out_code));
  dits_display \u_得分数字显示控制  (
    .in_1(cpu_1_io1), .in_2(cpu_1_instruction_out), .out_3({\得分数字显示控制_out_3_2 , \得分数字显示控制_out_3 }));
  CPU cpu_1 (
    .CLEAR(button_1_out), .KeyBorad_IN(keybroad_1_out_code), .IO1(cpu_1_io1), .IO2(cpu_1_io2),
    .Instruction_out(cpu_1_instruction_out));
  instructionSet instructionset_1 (
    .\显卡缓存 (\instructionset_1_显卡缓存 ), .data_in(cpu_1_instruction_out), .\显卡读入 (\instructionset_1_显卡读入 ),
    .REVERSE(instructionset_1_reverse));
  Hex_Digit_Display hex_digit_display_1 (.value(\得分数字显示控制_out_3_2 ));  // open: dp
  screen \u_显示处理  (
    .IN_y(cpu_1_io1), .IN_x(cpu_1_io2), .IO_in(\instructionset_1_显卡读入 ), .X(\显示处理_x ), .UP(\显示处理_up ),
    .DOWN(\显示处理_down ));
  Button button_2 (.out(button_2_out));
  Button button_3 (.out(button_3_out));
  Button button_4 (.out(button_4_out));
  Hex_Digit_Display hex_digit_display_2 (.value(\得分数字显示控制_out_3 ));  // open: dp
  screen_deriver \u_屏幕驱动  (
    .IO_Y(\显示处理_up ), .IO_X(\显示处理_x ), .reverse(instructionset_1_reverse), .CLR(\instructionset_1_显卡缓存 ),
    .OUT_1(\屏幕驱动_out_1 ), .OUT_2(\屏幕驱动_out_2 ), .OUT_3(\屏幕驱动_out_3 ), .OUT_4(\屏幕驱动_out_4 ));
  screen_deriver \u_屏幕驱动_2  (
    .IO_Y(\显示处理_down ), .IO_X(\显示处理_x ), .reverse(instructionset_1_reverse), .CLR(\instructionset_1_显卡缓存 ),
    .OUT_1(\屏幕驱动_2_out_1 ), .OUT_2(\屏幕驱动_2_out_2 ), .OUT_3(\屏幕驱动_2_out_3 ), .OUT_4(\屏幕驱动_2_out_4 ));
  Button button_5 (.out(button_5_out));
  DotMatrix #(.matrixcols(8), .matrixrows(8)) dotmatrix_1 (
    .col0(screen_interface_1_out_3), .col1(screen_interface_1_out_4), .col2(screen_interface_1_out_5),
    .col3(screen_interface_1_out_6), .col4(screen_interface_1_out_7), .col5(screen_interface_1_out_8),
    .col6(screen_interface_1_out_9), .col7(screen_interface_1_out_10));
  screen_interface screen_interface_1 (
    .out_3(screen_interface_1_out_3), .out_4(screen_interface_1_out_4), .out_5(screen_interface_1_out_5),
    .out_6(screen_interface_1_out_6), .out_7(screen_interface_1_out_7), .out_8(screen_interface_1_out_8),
    .out_9(screen_interface_1_out_9), .out_10(screen_interface_1_out_10), .in_1(\屏幕驱动_out_1 ),
    .in_2(\屏幕驱动_out_2 ));
  DotMatrix #(.matrixcols(8), .matrixrows(8)) dotmatrix_2 (
    .col0(screen_interface_2_out_3), .col1(screen_interface_2_out_4), .col2(screen_interface_2_out_5),
    .col3(screen_interface_2_out_6), .col4(screen_interface_2_out_7), .col5(screen_interface_2_out_8),
    .col6(screen_interface_2_out_9), .col7(screen_interface_2_out_10));
  screen_interface screen_interface_2 (
    .out_3(screen_interface_2_out_3), .out_4(screen_interface_2_out_4), .out_5(screen_interface_2_out_5),
    .out_6(screen_interface_2_out_6), .out_7(screen_interface_2_out_7), .out_8(screen_interface_2_out_8),
    .out_9(screen_interface_2_out_9), .out_10(screen_interface_2_out_10), .in_1(\屏幕驱动_2_out_1 ),
    .in_2(\屏幕驱动_2_out_2 ));
  DotMatrix #(.matrixcols(8), .matrixrows(8)) dotmatrix_3 (
    .col0(screen_interface_3_out_3), .col1(screen_interface_3_out_4), .col2(screen_interface_3_out_5),
    .col3(screen_interface_3_out_6), .col4(screen_interface_3_out_7), .col5(screen_interface_3_out_8),
    .col6(screen_interface_3_out_9), .col7(screen_interface_3_out_10));
  screen_interface screen_interface_3 (
    .out_3(screen_interface_3_out_3), .out_4(screen_interface_3_out_4), .out_5(screen_interface_3_out_5),
    .out_6(screen_interface_3_out_6), .out_7(screen_interface_3_out_7), .out_8(screen_interface_3_out_8),
    .out_9(screen_interface_3_out_9), .out_10(screen_interface_3_out_10), .in_1(\屏幕驱动_out_3 ),
    .in_2(\屏幕驱动_out_4 ));
  screen_interface screen_interface_4 (
    .out_3(screen_interface_4_out_3), .out_4(screen_interface_4_out_4), .out_5(screen_interface_4_out_5),
    .out_6(screen_interface_4_out_6), .out_7(screen_interface_4_out_7), .out_8(screen_interface_4_out_8),
    .out_9(screen_interface_4_out_9), .out_10(screen_interface_4_out_10), .in_1(\屏幕驱动_2_out_3 ),
    .in_2(\屏幕驱动_2_out_4 ));
  DotMatrix #(.matrixcols(8), .matrixrows(8)) dotmatrix_4 (
    .col0(screen_interface_4_out_3), .col1(screen_interface_4_out_4), .col2(screen_interface_4_out_5),
    .col3(screen_interface_4_out_6), .col4(screen_interface_4_out_7), .col5(screen_interface_4_out_8),
    .col6(screen_interface_4_out_9), .col7(screen_interface_4_out_10));

  // Notes on the sheet:
  //   复位
  //   键盘驱动
  //   CPU
  //   控制键
endmodule

module registerGroup (
  input  [4:0] ADDR,
  input  [4:0] ADDR2,
  input  [7:0] IN,
  input  [4:0] WRITE_ADDR,
  input  Clear,
  input  WRITE_EN,
  input  CLOCK,
  output [7:0] OUT_1,
  output [7:0] OUT_2,
  output [7:0] IO_6,
  output [7:0] IO_5
);

  wire and_1_out, and_2_out, and_3_out, and_4_out, and_5_out, and_6_out, and_7_out, decoder_1_out0,
       decoder_1_out1, decoder_1_out2, decoder_1_out3, decoder_1_out4, decoder_1_out5, decoder_1_out6,
       decoder_1_out7, undriven;
  wire [7:0] register_1_q, register_2_q, register_3_q, register_4_q, register_5_q, register_8_q;

  Decoder #(.select(3), .enable("false")) decoder_1 (
    .out0(decoder_1_out0), .out1(decoder_1_out1), .out2(decoder_1_out2), .out3(decoder_1_out3),
    .out4(decoder_1_out4), .out5(decoder_1_out5), .out6(decoder_1_out6), .out7(decoder_1_out7),
    .sel(WRITE_ADDR[2:0]));
  and and_1 (and_1_out, decoder_1_out0, WRITE_EN);
  and and_2 (and_2_out, decoder_1_out1, WRITE_EN);
  and and_3 (and_3_out, decoder_1_out2, WRITE_EN);
  and and_4 (and_4_out, decoder_1_out3, WRITE_EN);
  and and_5 (and_5_out, decoder_1_out4, WRITE_EN);
  and and_6 (and_6_out, decoder_1_out5, WRITE_EN);
  and and_7 (and_7_out, decoder_1_out6, WRITE_EN);
  // AND_Gate and_8 has open pins: in0=decoder_1_out7, in1=WRITE_EN, out=open
  Register register_1 (.D(IN), .en(and_1_out), .Q(register_1_q), .clk(CLOCK), .clr(Clear));
  Register register_2 (.D(IN), .en(and_2_out), .Q(register_2_q), .clk(CLOCK), .clr(Clear));
  Register register_3 (.D(IN), .en(and_3_out), .Q(register_3_q), .clk(CLOCK), .clr(Clear));
  Register register_4 (.D(IN), .en(and_4_out), .Q(register_4_q), .clk(CLOCK), .clr(Clear));
  Register register_5 (.D(IN), .en(and_5_out), .Q(register_5_q), .clk(CLOCK), .clr(Clear));
  Register register_6 (.D(IN), .en(and_6_out), .Q(IO_5), .clk(CLOCK), .clr(Clear));
  Register register_7 (.D(IN), .en(and_7_out), .Q(IO_6), .clk(CLOCK), .clr(Clear));
  Register register_8 (.en(undriven), .Q(register_8_q), .clk(undriven), .clr(1'b1));  // open: D
  Multiplexer #(.select(3), .width(8), .enable("false")) multiplexer_1 (
    .in0(register_1_q), .in1(register_2_q), .in2(register_3_q), .in3(register_4_q), .in4(register_5_q),
    .in5(IO_5), .in6(IO_6), .in7(register_8_q), .out(OUT_1), .sel(ADDR[2:0]));
  Multiplexer #(.select(3), .width(8), .enable("false")) multiplexer_2 (
    .in0(register_1_q), .in1(register_2_q), .in2(register_3_q), .in3(register_4_q), .in4(register_5_q),
    .in5(IO_5), .in6(IO_6), .in7(register_8_q), .out(OUT_2), .sel(ADDR2[2:0]));
endmodule

module AU (
  input  CRT,
  input  [7:0] IN_A,
  input  [7:0] IN_B,
  output [7:0] OUT
);

  wire [7:0] adder_1_out, multiplexer_1_out, not_1_out;

  assign not_1_out = ~IN_B;  // NOT_Gate not_1, 8 bits wide
  Adder adder_1 (.a(not_1_out), .b(8'h1), .out(adder_1_out));  // open: cin, cout
  Multiplexer #(.width(8), .enable("false")) multiplexer_1 (
    .in0(adder_1_out), .in1(IN_B), .out(multiplexer_1_out), .sel(CRT));
  Adder adder_2 (.a(IN_A), .b(multiplexer_1_out), .out(OUT));  // open: cin, cout
endmodule

module LU (
  input  CRT,
  input  [7:0] IN_A,
  input  [7:0] IN_B,
  output [7:0] OUT
);

  wire [7:0] and_1_out, or_1_out;

  assign and_1_out = IN_A & IN_B;  // AND_Gate and_1, 8 bits wide
  assign or_1_out = IN_A | IN_B;  // OR_Gate or_1, 8 bits wide
  Multiplexer #(.width(8), .enable("false")) multiplexer_1 (.in0(and_1_out), .in1(or_1_out), .out(OUT), .sel(CRT));
endmodule

module ALU (
  input  [5:0] CRT,
  input  [7:0] IN_A,
  input  [7:0] IN_B,
  output [7:0] out_4
);

  wire [7:0] and_1_out, and_2_out, au_1_out, lu_1_out, multiplexer_1_out, not_1_out, not_2_out, or_1_out;

  assign or_1_out = IN_A | IN_B;  // OR_Gate or_1, 8 bits wide
  assign and_1_out = IN_B & IN_A;  // AND_Gate and_1, 8 bits wide
  assign not_1_out = ~and_1_out;  // NOT_Gate not_1, 8 bits wide
  AU au_1 (.CRT(CRT[2]), .IN_A(IN_A), .IN_B(IN_B), .OUT(au_1_out));
  LU lu_1 (.CRT(CRT[3]), .IN_A(IN_A), .IN_B(IN_B), .OUT(lu_1_out));
  Multiplexer #(.width(8), .enable("false")) multiplexer_1 (
    .in0(lu_1_out), .in1(au_1_out), .out(multiplexer_1_out), .sel(CRT[1]));
  Multiplexer #(.width(8), .enable("false")) multiplexer_2 (
    .in0(multiplexer_1_out), .in1(not_2_out), .out(out_4), .sel(CRT[0]));
  assign and_2_out = or_1_out & not_1_out;  // AND_Gate and_2, 8 bits wide
  assign not_2_out = ~and_2_out;  // NOT_Gate not_2, 8 bits wide

  // Notes on the sheet:
  //   用取反+异或获取是否相等
endmodule

module RAM (
  input  [31:0] CODE,
  input  CLEAR,
  output [7:0] Jump,
  output [7:0] IO_6,
  output [7:0] IO_5
);

  wire clock_1_out, clock_2_out, not_1_out;
  wire [7:0] alu_1_out_4, bit_extender_1_out, multiplexer_1_out, multiplexer_2_out, multiplexer_3_out,
       ram_1_data, registergroup_1_out_1, registergroup_1_out_2;

  registerGroup registergroup_1 (
    .ADDR(CODE[25:21]), .IN(multiplexer_1_out), .WRITE_EN(CODE[31]), .CLOCK(clock_1_out),
    .OUT_1(registergroup_1_out_1), .WRITE_ADDR(CODE[20:16]), .Clear(CLEAR), .OUT_2(registergroup_1_out_2),
    .ADDR2(CODE[20:16]), .IO_6(IO_6), .IO_5(IO_5));
  Clock clock_1 (.out(clock_1_out));
  Bit_Extender #(.in_width(10), .out_width(8)) bit_extender_1 (.in(CODE[15:6]), .out(bit_extender_1_out));
  Multiplexer #(.width(8), .enable("false")) multiplexer_1 (
    .in0(alu_1_out_4), .in1(ram_1_data), .out(multiplexer_1_out), .sel(CODE[30]));
  Multiplexer #(.width(8), .enable("false")) multiplexer_2 (
    .in0(registergroup_1_out_1), .in1(IO_5), .out(multiplexer_2_out), .sel(CODE[4]));
  Multiplexer #(.width(8), .enable("false")) multiplexer_3 (
    .in0(bit_extender_1_out), .in1(IO_6), .out(multiplexer_3_out), .sel(CODE[4]));
  ALU alu_1 (.CRT(CODE[5:0]), .IN_A(multiplexer_2_out), .IN_B(multiplexer_3_out), .out_4(alu_1_out_4));
  not not_1 (not_1_out, CODE[29]);
  Multiplexer #(.width(8), .enable("false")) multiplexer_4 (
    .in0({8{1'b0}}), .in1(alu_1_out_4), .out(Jump), .sel(CODE[28]));
  Clock clock_2 (.out(clock_2_out));
  RAM_part #(.bus("separate")) ram_1 (
    .addr(alu_1_out_4), .din(registergroup_1_out_2), .data(ram_1_data), .str(CODE[29]), .clk(clock_2_out),
    .ld(not_1_out), .clr(CLEAR));  // open: sel
endmodule

module piont (
  input  [31:0] in_1,
  input  in_2,
  input  CLEAR,
  output [15:0] OUT
);

  wire clock_1_out;
  wire [15:0] bit_extender_1_out, multiplexer_1_out, register_1_q;

  Clock clock_1 (.out(clock_1_out));
  Multiplexer #(.width(16), .enable("false")) multiplexer_1 (
    .in0(OUT), .in1(bit_extender_1_out), .out(multiplexer_1_out), .sel(in_2));
  Register #(.width(16)) register_1 (
    .D(multiplexer_1_out), .Q(register_1_q), .clk(clock_1_out), .clr(CLEAR));  // open: en
  Adder #(.width(16)) adder_1 (.a(register_1_q), .b(16'h1), .out(OUT));  // open: cin, cout
  assign bit_extender_1_out = {{9{1'b0}}, in_1[20:14]};  // Bit_Extender bit_extender_1
endmodule

module screen (
  input  [7:0] IN_y,
  input  [7:0] IN_x,
  input  IO_in,
  output [7:0] UP,
  output [7:0] DOWN,
  output [3:0] X
);

  wire [3:0] bit_extender_1_out;
  wire [7:0] multiplexer_1_out;
  wire [15:0] shifter_1_out;

  Multiplexer #(.width(8), .enable("false")) multiplexer_1 (
    .in0({8{1'b0}}), .in1(IN_x), .out(multiplexer_1_out), .sel(IO_in));
  Bit_Extender #(.out_width(4)) bit_extender_1 (.in(IN_y), .out(bit_extender_1_out));
  Bit_Extender #(.out_width(4)) bit_extender_2 (.in(multiplexer_1_out), .out(X));
  Shifter #(.width(16)) shifter_1 (.in(16'h1), .\dist (bit_extender_1_out), .out(shifter_1_out));
  Multiplexer #(.width(16), .enable("false")) multiplexer_2 (
    .in0({16{1'b0}}), .in1(shifter_1_out), .out({UP, DOWN}), .sel(IO_in));
endmodule

module keybroad (
  input  BTN_UP,
  input  BTN_LEFT,
  input  BTN_right,
  input  BTN_DOWN,
  output [31:0] OUT_CODE
);

  wire clock_1_out, or_1_out;
  wire [2:0] multiplexer_1_out, multiplexer_2_out, multiplexer_3_out, multiplexer_4_out, register_1_q;

  Clock clock_1 (.out(clock_1_out));
  Register #(.width(3)) register_1 (
    .D(multiplexer_1_out), .en(or_1_out), .Q(register_1_q), .clk(clock_1_out));  // open: clr
  ROM #(.addrWidth(3), .dataWidth(32)) rom_1 (.addr(register_1_q), .data(OUT_CODE));  // open: sel
  or or_1 (or_1_out, BTN_LEFT, BTN_DOWN, BTN_UP, BTN_right);
  Multiplexer #(.width(3), .enable("false")) multiplexer_1 (
    .in0(multiplexer_3_out), .in1(3'b100), .out(multiplexer_1_out), .sel(BTN_LEFT));
  Multiplexer #(.width(3), .enable("false")) multiplexer_2 (
    .in0(multiplexer_4_out), .in1(3'b001), .out(multiplexer_2_out), .sel(BTN_UP));
  Multiplexer #(.width(3), .enable("false")) multiplexer_3 (
    .in0(multiplexer_2_out), .in1(3'b010), .out(multiplexer_3_out), .sel(BTN_DOWN));
  Multiplexer #(.width(3), .enable("false")) multiplexer_4 (
    .in0(3'b000), .in1(3'b011), .out(multiplexer_4_out), .sel(BTN_right));

  // Notes on the sheet:
  //   contents of rom_1 (hex, n*v repeats v):
  //   0 80000046 8000ffc6 80210046 8021ffc6
endmodule

module CPU (
  input  CLEAR,
  input  [31:0] KeyBorad_IN,
  output [7:0] IO1,
  output [7:0] IO2,
  output [15:0] Instruction_out
);

  wire and_1_out, and_2_out, and_3_out, and_4_out, and_5_out, clock_1_out, not_1_out;
  wire [5:0] rom_1_data;
  wire [7:0] ram_1_jump, random_1_out;
  wire [13:6] rom_1_data_2;
  wire [15:0] piont_1_out, subtractor_1_out;
  wire [17:0] rom_1_data_3;
  wire [31:0] multiplexer_1_out, multiplexer_2_out, multiplexer_3_out;

  Subtractor #(.width(16)) subtractor_1 (.a(piont_1_out), .b(16'h1), .out(subtractor_1_out));  // open: bin, bout
  Clock clock_1 (.out(clock_1_out));
  piont piont_1 (.OUT(piont_1_out), .in_1({rom_1_data_3, rom_1_data_2, rom_1_data}), .in_2(and_1_out), .CLEAR(CLEAR));
  ROM #(.addrWidth(16), .dataWidth(32)) rom_1 (
    .addr(subtractor_1_out), .data({rom_1_data_3, rom_1_data_2, rom_1_data}));  // open: sel
  Random random_1 (.clk(clock_1_out), .next(and_2_out), .out(random_1_out));  // open: clr
  and and_1 (and_1_out, rom_1_data_3[14], and_4_out);
  and and_2 (and_2_out, rom_1_data[0], rom_1_data[1]);
  Multiplexer #(.width(32), .enable("false")) multiplexer_1 (
    .in0({32{1'b0}}), .in1({rom_1_data_3, random_1_out, rom_1_data}), .out(multiplexer_1_out), .sel(and_2_out));
  Multiplexer #(.width(32), .enable("false")) multiplexer_2 (
    .in0(multiplexer_1_out), .in1(KeyBorad_IN), .out(multiplexer_2_out), .sel(rom_1_data[0]));
  Multiplexer #(.width(32), .enable("false")) multiplexer_3 (
    .in0({rom_1_data_3, rom_1_data_2, rom_1_data}), .in1(multiplexer_2_out), .out(multiplexer_3_out),
    .sel(rom_1_data_3[12]));
  not not_1 (not_1_out, and_5_out);
  and and_3 (and_3_out, rom_1_data_3[12], not_1_out);
  Multiplexer #(.width(16), .enable("false")) multiplexer_4 (
    .in0({16{1'b0}}), .in1({rom_1_data_3[1:0], rom_1_data_2, rom_1_data}), .out(Instruction_out),
    .sel(and_3_out));
  and and_4 (and_4_out, ram_1_jump[0], ram_1_jump[1], ram_1_jump[2], ram_1_jump[3], ram_1_jump[4], ram_1_jump[5], ram_1_jump[6], ram_1_jump[7]);
  and and_5 (and_5_out, rom_1_data[0], rom_1_data[1], rom_1_data[2], rom_1_data[3]);
  RAM ram_1 (.CODE(multiplexer_3_out), .IO_6(IO2), .IO_5(IO1), .CLEAR(CLEAR), .Jump(ram_1_jump));

  // Notes on the sheet:
  //   contents of rom_1 (hex, n*v repeats v):
  //   80e00006 80e10006 20e00006 20e10046 c0e00106 c0e10146 20e00186 20e101c6 c0e00086 c0e100c6 20e00106
  //   20e10146 c0e00006 c0e10046 20e00086 20e100c6 4000001 20e00006 20e10046 c0e50186 c0e601c6 4004000
  //   c0e50006 c0e60046 4008000 c0e50246 c0e60186 10074011 10eb3fc8 c0e60286 c0e501c6 10084011 10eb3fc8
  //   c0e50206 80a50046 20e50206 4000020 c0e50246 4004000 84050003 84060003 20e50246 20e60286 4008000
  //   10e13fc8
endmodule

module instructionSet (
  input  [15:0] data_in,
  output REVERSE,
  output \显卡缓存 ,
  output \显卡读入 
);

  or or_1 (\显卡读入 , data_in[15], data_in[14]);
  and and_1 (\显卡缓存 , data_in[15], data_in[14]);

  assign REVERSE = data_in[14];
endmodule

module screen_deriver (
  input  [7:0] IO_Y,
  input  [3:0] IO_X,
  input  reverse,
  input  CLR,
  output [31:0] OUT_1,
  output [31:0] OUT_2,
  output [31:0] OUT_3,
  output [31:0] OUT_4
);

  wire clock_1_out, clock_2_out, clock_3_out, clock_4_out, decoder_1_out0, decoder_1_out1, decoder_1_out2,
       decoder_1_out3, decoder_1_out4, decoder_1_out5, decoder_1_out6, decoder_1_out7, decoder_1_out8,
       decoder_1_out9, decoder_1_out10, decoder_1_out11, decoder_1_out12, decoder_1_out13, decoder_1_out14,
       decoder_1_out15;
  wire [7:0] multiplexer_1_out, multiplexer_2_out, multiplexer_3_out, multiplexer_4_out, multiplexer_5_out,
       multiplexer_6_out, multiplexer_7_out, multiplexer_8_out, multiplexer_9_out, multiplexer_10_out,
       multiplexer_11_out, multiplexer_12_out, multiplexer_13_out, multiplexer_14_out, multiplexer_15_out,
       multiplexer_16_out;
  wire [31:0] and_1_out, and_2_out, and_3_out, and_4_out, multiplexer_17_out, multiplexer_18_out,
       multiplexer_19_out, multiplexer_20_out, not_1_out, not_2_out, not_3_out, not_4_out, or_1_out,
       or_2_out, or_3_out, or_4_out;

  Decoder #(.select(4), .disabled(0), .enable("false")) decoder_1 (
    .out0(decoder_1_out0), .out1(decoder_1_out1), .out2(decoder_1_out2), .out3(decoder_1_out3),
    .out4(decoder_1_out4), .out5(decoder_1_out5), .out6(decoder_1_out6), .out7(decoder_1_out7),
    .out8(decoder_1_out8), .out9(decoder_1_out9), .out10(decoder_1_out10), .out11(decoder_1_out11),
    .out12(decoder_1_out12), .out13(decoder_1_out13), .out14(decoder_1_out14), .out15(decoder_1_out15),
    .sel(IO_X));
  Multiplexer #(.width(8), .enable("false")) multiplexer_1 (
    .in0({8{1'b0}}), .in1(IO_Y), .out(multiplexer_1_out), .sel(decoder_1_out0));
  Multiplexer #(.width(8), .enable("false")) multiplexer_2 (
    .in0({8{1'b0}}), .in1(IO_Y), .out(multiplexer_2_out), .sel(decoder_1_out1));
  Multiplexer #(.width(8), .enable("false")) multiplexer_3 (
    .in0({8{1'b0}}), .in1(IO_Y), .out(multiplexer_3_out), .sel(decoder_1_out2));
  Multiplexer #(.width(8), .enable("false")) multiplexer_4 (
    .in0({8{1'b0}}), .in1(IO_Y), .out(multiplexer_4_out), .sel(decoder_1_out3));
  Multiplexer #(.width(8), .enable("false")) multiplexer_5 (
    .in0({8{1'b0}}), .in1(IO_Y), .out(multiplexer_5_out), .sel(decoder_1_out4));
  Multiplexer #(.width(8), .enable("false")) multiplexer_6 (
    .in0({8{1'b0}}), .in1(IO_Y), .out(multiplexer_6_out), .sel(decoder_1_out5));
  Multiplexer #(.width(8), .enable("false")) multiplexer_7 (
    .in0({8{1'b0}}), .in1(IO_Y), .out(multiplexer_7_out), .sel(decoder_1_out6));
  Multiplexer #(.width(8), .enable("false")) multiplexer_8 (
    .in0({8{1'b0}}), .in1(IO_Y), .out(multiplexer_8_out), .sel(decoder_1_out7));
  Multiplexer #(.width(8), .enable("false")) multiplexer_9 (
    .in0({8{1'b0}}), .in1(IO_Y), .out(multiplexer_9_out), .sel(decoder_1_out8));
  Multiplexer #(.width(8), .enable("false")) multiplexer_10 (
    .in0({8{1'b0}}), .in1(IO_Y), .out(multiplexer_10_out), .sel(decoder_1_out9));
  Multiplexer #(.width(8), .enable("false")) multiplexer_11 (
    .in0({8{1'b0}}), .in1(IO_Y), .out(multiplexer_11_out), .sel(decoder_1_out10));
  Multiplexer #(.width(8), .enable("false")) multiplexer_12 (
    .in0({8{1'b0}}), .in1(IO_Y), .out(multiplexer_12_out), .sel(decoder_1_out11));
  Multiplexer #(.width(8), .enable("false")) multiplexer_13 (
    .in0({8{1'b0}}), .in1(IO_Y), .out(multiplexer_13_out), .sel(decoder_1_out12));
  Multiplexer #(.width(8), .enable("false")) multiplexer_14 (
    .in0({8{1'b0}}), .in1(IO_Y), .out(multiplexer_14_out), .sel(decoder_1_out13));
  Multiplexer #(.width(8), .enable("false")) multiplexer_15 (
    .in0({8{1'b0}}), .in1(IO_Y), .out(multiplexer_15_out), .sel(decoder_1_out14));
  Multiplexer #(.width(8), .enable("false")) multiplexer_16 (
    .in0({8{1'b0}}), .in1(IO_Y), .out(multiplexer_16_out), .sel(decoder_1_out15));
  assign not_1_out = ~{multiplexer_4_out, multiplexer_3_out, multiplexer_2_out, multiplexer_1_out};  // NOT_Gate not_1, 32 bits wide
  assign or_1_out = OUT_2 | {multiplexer_8_out, multiplexer_7_out, multiplexer_6_out, multiplexer_5_out};  // OR_Gate or_1, 32 bits wide
  assign not_2_out = ~{multiplexer_8_out, multiplexer_7_out, multiplexer_6_out, multiplexer_5_out};  // NOT_Gate not_2, 32 bits wide
  assign not_3_out = ~{multiplexer_16_out, multiplexer_15_out, multiplexer_14_out, multiplexer_13_out};  // NOT_Gate not_3, 32 bits wide
  assign or_2_out = OUT_1 | {multiplexer_4_out, multiplexer_3_out, multiplexer_2_out, multiplexer_1_out};  // OR_Gate or_2, 32 bits wide
  Multiplexer #(.width(32), .enable("false")) multiplexer_17 (
    .in0(or_2_out), .in1(and_1_out), .out(multiplexer_17_out), .sel(reverse));
  assign and_1_out = OUT_1 & not_1_out;  // AND_Gate and_1, 32 bits wide
  Multiplexer #(.width(32), .enable("false")) multiplexer_18 (
    .in0(or_1_out), .in1(and_2_out), .out(multiplexer_18_out), .sel(reverse));
  assign and_2_out = OUT_2 & not_2_out;  // AND_Gate and_2, 32 bits wide
  assign not_4_out = ~{multiplexer_12_out, multiplexer_11_out, multiplexer_10_out, multiplexer_9_out};  // NOT_Gate not_4, 32 bits wide
  assign and_3_out = not_4_out & OUT_3;  // AND_Gate and_3, 32 bits wide
  Multiplexer #(.width(32), .enable("false")) multiplexer_19 (
    .in0(or_3_out), .in1(and_3_out), .out(multiplexer_19_out), .sel(reverse));
  assign or_3_out = OUT_3 | {multiplexer_12_out, multiplexer_11_out, multiplexer_10_out, multiplexer_9_out};  // OR_Gate or_3, 32 bits wide
  Clock clock_1 (.out(clock_1_out));
  assign or_4_out = OUT_4 | {multiplexer_16_out, multiplexer_15_out, multiplexer_14_out, multiplexer_13_out};  // OR_Gate or_4, 32 bits wide
  assign and_4_out = OUT_4 & not_3_out;  // AND_Gate and_4, 32 bits wide
  Register #(.width(32)) register_1 (.D(multiplexer_17_out), .Q(OUT_1), .clk(clock_2_out), .clr(CLR));  // open: en
  Clock clock_2 (.out(clock_2_out));
  Register #(.width(32)) register_2 (.D(multiplexer_18_out), .Q(OUT_2), .clk(clock_3_out), .clr(CLR));  // open: en
  Clock clock_3 (.out(clock_3_out));
  Register #(.width(32)) register_3 (.D(multiplexer_19_out), .Q(OUT_3), .clk(clock_1_out), .clr(CLR));  // open: en
  Multiplexer #(.width(32), .enable("false")) multiplexer_20 (
    .in0(or_4_out), .in1(and_4_out), .out(multiplexer_20_out), .sel(reverse));
  Register #(.width(32)) register_4 (.D(multiplexer_20_out), .Q(OUT_4), .clk(clock_4_out), .clr(CLR));  // open: en
  Clock clock_4 (.out(clock_4_out));
endmodule

module screen_interface (
  input  [31:0] in_1,
  input  [31:0] in_2,
  output [7:0] out_3,
  output [7:0] out_4,
  output [7:0] out_5,
  output [7:0] out_6,
  output [7:0] out_7,
  output [7:0] out_8,
  output [7:0] out_9,
  output [7:0] out_10
);


  assign out_3 = in_1[7:0];
  assign out_4 = in_1[15:8];
  assign out_5 = in_1[23:16];
  assign out_6 = in_1[31:24];
  assign out_7 = in_2[7:0];
  assign out_8 = in_2[15:8];
  assign out_9 = in_2[23:16];
  assign out_10 = in_2[31:24];
endmodule

module dits_display (
  input  [7:0] in_1,
  input  [15:0] in_2,
  output [7:0] out_3
);

  wire clock_1_out;

  Register register_1 (.D(in_1), .en(in_2[5]), .Q(out_3), .clk(clock_1_out));  // open: clr
  Clock clock_1 (.out(clock_1_out));
endmodule
